// Logisim project COD_Project.circ as structural Verilog: 17 circuits, main circuit main
module main (
  input  AR_CLR,
  input  START,
  input  PC_CLR,
  input  DR_CLR,
  input  TR_INC,
  input  TR_LD,
  input  TR_CLR,
  input  SHL,
  input  SHR,
  input  [7:0] INPR,
  output E_out
);

  wire AC_clr, AC_inr, AC_load, AR_inr, AR_load, B0, clk, CLK_out, decoder_1_out0, decoder_1_out1,
       decoder_1_out2, decoder_1_out3, decoder_1_out4, decoder_1_out5, decoder_1_out6, decoder_1_out7,
       decoder_1_out8, decoder_1_out9, decoder_1_out10, decoder_1_out11, decoder_1_out12, decoder_1_out13,
       decoder_1_out14, decoder_1_out15, decoder_2_out0, decoder_2_out1, decoder_2_out2, decoder_2_out3,
       decoder_2_out4, decoder_2_out5, decoder_2_out6, decoder_2_out7, DR_inr, DR_load, E, E_clr,
       E_compliment, E_load, I, IR_load, Memory_read, Memory_write, PC_inr, PC_load, r, SC_clr;
  wire [2:0] P2_P1_P0, S2_S1_S0;
  wire [3:0] sequence_counter_1_sc_out;
  wire [11:0] AR_REG_address;
  wire [14:1] IR_OUT;
  wire [15:0] AC_OUT, AR_REG_data_out, Data_out, DR_OUT, multiplexer_1_out, PC_REG_data_out, ram_1_dout,
       TR_REG_outpt;

  Sequence_Counter sequence_counter_1 (
    .clr(SC_clr), .Start_pulse(START), .r(r), .clk(clk), .B0(B0), .SC_out(sequence_counter_1_sc_out));
  Decoder #(.select(4)) decoder_1 (
    .out0(decoder_1_out0), .out1(decoder_1_out1), .out2(decoder_1_out2), .out3(decoder_1_out3),
    .out4(decoder_1_out4), .out5(decoder_1_out5), .out6(decoder_1_out6), .out7(decoder_1_out7),
    .out8(decoder_1_out8), .out9(decoder_1_out9), .out10(decoder_1_out10), .out11(decoder_1_out11),
    .out12(decoder_1_out12), .out13(decoder_1_out13), .out14(decoder_1_out14), .out15(decoder_1_out15),
    .sel(sequence_counter_1_sc_out));  // open: en
  Decoder #(.select(3)) decoder_2 (
    .out0(decoder_2_out0), .out1(decoder_2_out1), .out2(decoder_2_out2), .out3(decoder_2_out3),
    .out4(decoder_2_out4), .out5(decoder_2_out5), .out6(decoder_2_out6), .out7(decoder_2_out7),
    .sel(IR_OUT[14:12]));  // open: en
  control_logic control_logic_1 (
    .I(I), .T0(decoder_1_out0), .T1(decoder_1_out1), .T2(decoder_1_out2), .T3(decoder_1_out3),
    .T4(decoder_1_out4), .T5(decoder_1_out5), .T6(decoder_1_out6), .T7(decoder_1_out7), .T8(decoder_1_out8),
    .T9(decoder_1_out9), .T10(decoder_1_out10), .T11(decoder_1_out11), .T12(decoder_1_out12),
    .T13(decoder_1_out13), .T14(decoder_1_out14), .T15(decoder_1_out15), .B0(B0), .B1(IR_OUT[1]),
    .B2(IR_OUT[2]), .B3(IR_OUT[3]), .B4(IR_OUT[4]), .B5(IR_OUT[5]), .B6(IR_OUT[6]), .B7(IR_OUT[7]),
    .B8(IR_OUT[8]), .B9(IR_OUT[9]), .B10(IR_OUT[10]), .B11(IR_OUT[11]), .D0(decoder_2_out0),
    .D1(decoder_2_out1), .D2(decoder_2_out2), .D3(decoder_2_out3), .D4(decoder_2_out4), .D5(decoder_2_out5),
    .D6(decoder_2_out6), .D7(decoder_2_out7), .E(E), .DR_in(DR_OUT), .AC_in(AC_OUT), .AR_load(AR_load),
    .DR_load(DR_load), .AC_load(AC_load), .AR_inr(AR_inr), .DR_inr(DR_inr), .AC_inr(AC_inr),
    .IR_load(IR_load), .AC_clr(AC_clr), .PC_inr(PC_inr), .PC_load(PC_load), .S2_S1_S0(S2_S1_S0),
    .Memory_read(Memory_read), .Memory_write(Memory_write), .SC_clr(SC_clr), .P2_P1_P0(P2_P1_P0),
    .E_clr(E_clr), .E_compliment(E_compliment), .E_load(E_load), .r(r));
  E_flip_flop e_flip_flop_1 (
    .E_load(E_load), .clk(clk), .E_compliment(E_compliment), .E_clr(E_clr), .E_inr(E), .E_out(E_out));
  Clock u_CLK (.out(CLK_out));
  AR AR_REG (
    .INC(AR_inr), .LD(AR_load), .CLR(AR_CLR), .CLK(CLK_out), .Data_in(multiplexer_1_out),
    .Address(AR_REG_address), .Data_out(AR_REG_data_out));
  PC PC_REG (
    .Data_in(multiplexer_1_out), .INR(PC_inr), .LD(PC_load), .CLR(PC_CLR), .CLK(CLK_out),
    .Data_out(PC_REG_data_out));
  DR DR_REG (.DATA_IN(multiplexer_1_out), .INC(DR_inr), .LD(DR_load), .CLR(DR_CLR), .CLK(CLK_out), .OUTPT(DR_OUT));
  AC AC_REG (.DATA_IN(Data_out), .INC(AC_inr), .LD(AC_load), .CLR(AC_clr), .CLK(CLK_out), .OUTPT(AC_OUT));
  IR IR_REG (.DATA_IN(multiplexer_1_out), .LD(IR_load), .CLK(CLK_out), .OUTPT({I, IR_OUT, B0}));
  TR TR_REG (.DATA_IN(multiplexer_1_out), .INC(TR_INC), .LD(TR_LD), .CLR(TR_CLR), .CLK(CLK_out), .OUTPT(TR_REG_outpt));
  ALU alu_1 (
    .DR(DR_OUT), .AC(AC_OUT), .CLK(CLK_out), .P2P1P0(P2_P1_P0), .SHL(SHL), .SHR(SHR), .INPR(INPR), .E(E),
    .DATA_OUT(Data_out));
  Clock clock_1 (.out(clk));
  Multiplexer #(.select(3), .width(16)) multiplexer_1 (
    .in1(AR_REG_data_out), .in2(PC_REG_data_out), .in3(DR_OUT), .in4(AC_OUT), .in5({I, IR_OUT, B0}),
    .in6(TR_REG_outpt), .in7(ram_1_dout), .out(multiplexer_1_out), .sel(S2_S1_S0));  // open: in0
  RAM #(.addrWidth(12), .asyncread("true"), .dataWidth(16)) ram_1 (
    .addr(AR_REG_address), .we(Memory_write), .oe(Memory_read), .clk(CLK_out), .din(multiplexer_1_out),
    .dout(ram_1_dout));

  // Other names for the same wires on the sheet: IR_OUT (some bits) = {I, B0}
endmodule

module AR (
  input  INC,
  input  LD,
  input  CLR,
  input  CLK,
  input  [15:0] Data_in,
  output [11:0] Address,
  output [15:0] Data_out
);

  wire [11:0] adder_1_out, multiplexer_1_out, multiplexer_2_out, multiplexer_3_out;

  Adder #(.width(12)) adder_1 (.a(12'h1), .b(Address), .out(adder_1_out));  // open: cin, cout
  Multiplexer #(.width(12)) multiplexer_1 (.in0(Address), .in1(adder_1_out), .out(multiplexer_1_out), .sel(INC));
  Multiplexer #(.width(12)) multiplexer_2 (
    .in0(multiplexer_1_out), .in1(Data_in[11:0]), .out(multiplexer_2_out), .sel(LD));
  Multiplexer #(.width(12)) multiplexer_3 (
    .in0(multiplexer_2_out), .in1({12{1'b0}}), .out(multiplexer_3_out), .sel(CLR));
  Register #(.width(12)) register_1 (.D(multiplexer_3_out), .clk(CLK), .Q(Address));  // open: en, clr

  assign Data_in[14:12] = {3{Data_in[15]}};
  assign Data_out = {4'b0000, Address};
  // also tied to GND on the sheet: Data_in[15]

  // Notes on the sheet:
  //   Akshat Patil
  //   23BIT246
endmodule

module Register_12 (
  input  [11:0] DATA_IN,
  input  INC,
  input  LD,
  input  CLR,
  input  CLK,
  output [11:0] OUTPT
);

  wire [11:0] adder_1_out, multiplexer_1_out, multiplexer_2_out, multiplexer_3_out;

  Adder #(.width(12)) adder_1 (.a(12'h1), .b(OUTPT), .out(adder_1_out));  // open: cin, cout
  Multiplexer #(.width(12)) multiplexer_1 (.in0(OUTPT), .in1(adder_1_out), .out(multiplexer_1_out), .sel(INC));
  Multiplexer #(.width(12)) multiplexer_2 (.in0(multiplexer_1_out), .in1(DATA_IN), .out(multiplexer_2_out), .sel(LD));
  Multiplexer #(.width(12)) multiplexer_3 (
    .in0(multiplexer_2_out), .in1({12{1'b0}}), .out(multiplexer_3_out), .sel(CLR));
  Register #(.width(12)) register_1 (.D(multiplexer_3_out), .clk(CLK), .Q(OUTPT));  // open: en, clr

  // Notes on the sheet:
  //   Akshat Patil
  //   23BIT246
endmodule

module PC (
  input  [15:0] Data_in,
  input  INR,
  input  LD,
  input  CLR,
  input  CLK,
  output [15:0] Data_out
);

  Register_12 register_12_1 (.DATA_IN(Data_in[11:0]), .INC(INR), .LD(LD), .CLR(CLR), .CLK(CLK), .OUTPT(Data_out[11:0]));

  assign Data_in[14:12] = {3{Data_in[15]}};
  assign Data_out[15:12] = 4'b0000;
  // also tied to GND on the sheet: Data_in[15]
endmodule

module AC (
  input  [15:0] DATA_IN,
  input  INC,
  input  LD,
  input  CLR,
  input  CLK,
  output [15:0] OUTPT
);

  wire [15:0] adder_1_out, multiplexer_1_out, multiplexer_2_out, multiplexer_3_out;

  Adder #(.width(16)) adder_1 (.a(16'h1), .b(OUTPT), .out(adder_1_out));  // open: cin, cout
  Multiplexer #(.width(16)) multiplexer_1 (.in0(OUTPT), .in1(adder_1_out), .out(multiplexer_1_out), .sel(INC));
  Multiplexer #(.width(16)) multiplexer_2 (.in0(multiplexer_1_out), .in1(DATA_IN), .out(multiplexer_2_out), .sel(LD));
  Multiplexer #(.width(16)) multiplexer_3 (
    .in0(multiplexer_2_out), .in1({16{1'b0}}), .out(multiplexer_3_out), .sel(CLR));
  Register #(.width(16)) register_1 (.D(multiplexer_3_out), .clk(CLK), .Q(OUTPT));  // open: en, clr

  // Notes on the sheet:
  //   Akshat Patil
  //   23BIT246
endmodule

module IR (
  input  [15:0] DATA_IN,
  input  LD,
  input  CLK,
  output [15:0] OUTPT
);

  wire [15:0] adder_1_out, multiplexer_1_out, multiplexer_2_out, multiplexer_3_out;

  Adder #(.width(16)) adder_1 (.a(16'h1), .b(OUTPT), .out(adder_1_out));  // open: cin, cout
  Multiplexer #(.width(16)) multiplexer_1 (.in0(OUTPT), .in1(adder_1_out), .out(multiplexer_1_out), .sel(1'b0));
  Multiplexer #(.width(16)) multiplexer_2 (.in0(multiplexer_1_out), .in1(DATA_IN), .out(multiplexer_2_out), .sel(LD));
  Multiplexer #(.width(16)) multiplexer_3 (
    .in0(multiplexer_2_out), .in1({16{1'b0}}), .out(multiplexer_3_out), .sel(1'b0));
  Register #(.width(16)) register_1 (.D(multiplexer_3_out), .clk(CLK), .Q(OUTPT));  // open: en, clr

  // Notes on the sheet:
  //   Akshat Patil
  //   23BIT246
endmodule

module DR (
  input  [15:0] DATA_IN,
  input  INC,
  input  LD,
  input  CLR,
  input  CLK,
  output [15:0] OUTPT
);

  wire [15:0] adder_1_out, multiplexer_1_out, multiplexer_2_out, multiplexer_3_out;

  Adder #(.width(16)) adder_1 (.a(16'h1), .b(OUTPT), .out(adder_1_out));  // open: cin, cout
  Multiplexer #(.width(16)) multiplexer_1 (.in0(OUTPT), .in1(adder_1_out), .out(multiplexer_1_out), .sel(INC));
  Multiplexer #(.width(16)) multiplexer_2 (.in0(multiplexer_1_out), .in1(DATA_IN), .out(multiplexer_2_out), .sel(LD));
  Multiplexer #(.width(16)) multiplexer_3 (
    .in0(multiplexer_2_out), .in1({16{1'b0}}), .out(multiplexer_3_out), .sel(CLR));
  Register #(.width(16)) register_1 (.D(multiplexer_3_out), .clk(CLK), .Q(OUTPT));  // open: en, clr

  // Notes on the sheet:
  //   Akshat Patil
  //   23BIT246
endmodule

module TR (
  input  [15:0] DATA_IN,
  input  INC,
  input  LD,
  input  CLR,
  input  CLK,
  output [15:0] OUTPT
);

  wire [15:0] adder_1_out, multiplexer_1_out, multiplexer_2_out, multiplexer_3_out;

  Adder #(.width(16)) adder_1 (.a(16'h1), .b(OUTPT), .out(adder_1_out));  // open: cin, cout
  Multiplexer #(.width(16)) multiplexer_1 (.in0(OUTPT), .in1(adder_1_out), .out(multiplexer_1_out), .sel(INC));
  Multiplexer #(.width(16)) multiplexer_2 (.in0(multiplexer_1_out), .in1(DATA_IN), .out(multiplexer_2_out), .sel(LD));
  Multiplexer #(.width(16)) multiplexer_3 (
    .in0(multiplexer_2_out), .in1({16{1'b0}}), .out(multiplexer_3_out), .sel(CLR));
  Register #(.width(16)) register_1 (.D(multiplexer_3_out), .clk(CLK), .Q(OUTPT));  // open: en, clr

  // Notes on the sheet:
  //   Akshat Patil
  //   23BIT246
endmodule

module ALU (
  input  [15:0] DR,
  input  [15:0] AC,
  input  CLK,
  input  [2:0] P2P1P0,
  input  SHL,
  input  SHR,
  input  [7:0] INPR,
  output E,
  output [15:0] DATA_OUT
);

  wire adder_1_cout;
  wire [15:0] adder_1_out, and_1_out, not_1_out;

  Register #(.width(1)) register_1 (.D(adder_1_cout), .en(1'b1), .clk(CLK), .Q(E));  // open: clr
  assign and_1_out = DR & AC;  // AND_Gate and_1, 16 bits wide
  Adder #(.width(16)) adder_1 (.a(DR), .b(AC), .out(adder_1_out), .cin(1'b0), .cout(adder_1_cout));
  assign not_1_out = ~AC;  // NOT_Gate not_1, 16 bits wide
  Multiplexer #(.select(3), .width(16)) multiplexer_1 (
    .in0(AC), .in1(and_1_out), .in2(adder_1_out), .in3(DR), .in4(not_1_out), .in5({SHR, AC[15:1]}),
    .in6({AC[14:0], SHL}), .in7({{8{1'b0}}, INPR}), .out(DATA_OUT), .sel(P2P1P0));
endmodule

module shift_l (
  input  SHL,
  input  [15:0] AC_in,
  output [15:0] AC
);


  assign AC = {AC_in[14:0], SHL};
endmodule

module shift_r (
  input  [15:0] inpt,
  input  SHR,
  output [15:0] opt
);


  assign opt = {SHR, inpt[15:1]};
endmodule

module Register_8 (
  input  [7:0] DATA_IN,
  input  INC,
  input  LD,
  input  CLR,
  input  CLK,
  output [7:0] OUTPT
);

  wire [7:0] adder_1_out, multiplexer_1_out, multiplexer_2_out, multiplexer_3_out;

  Adder adder_1 (.a(8'h1), .b(OUTPT), .out(adder_1_out));  // open: cin, cout
  Multiplexer #(.width(8)) multiplexer_1 (.in0(OUTPT), .in1(adder_1_out), .out(multiplexer_1_out), .sel(INC));
  Multiplexer #(.width(8)) multiplexer_2 (.in0(multiplexer_1_out), .in1(DATA_IN), .out(multiplexer_2_out), .sel(LD));
  Multiplexer #(.width(8)) multiplexer_3 (.in0(multiplexer_2_out), .in1({8{1'b0}}), .out(multiplexer_3_out), .sel(CLR));
  Register register_1 (.D(multiplexer_3_out), .clk(CLK), .Q(OUTPT));  // open: en, clr

  // Notes on the sheet:
  //   Akshat Patil
  //   23BIT246
endmodule

module INPR (
  input  [15:0] Data_in,
  input  load,
  input  clk,
  output [15:0] Data_out
);

  Register_8 register_8_1 (.DATA_IN(Data_in[7:0]), .LD(load), .CLK(clk), .OUTPT(Data_out[7:0]));  // open: INC, CLR
endmodule

module control_logic (
  input  I,
  input  T0,
  input  T1,
  input  T2,
  input  T3,
  input  T4,
  input  T5,
  input  T6,
  input  T7,
  input  T8,
  input  T9,
  input  T10,
  input  T11,
  input  T12,
  input  T13,
  input  T14,
  input  T15,
  input  B0,
  input  B1,
  input  B2,
  input  B3,
  input  B4,
  input  B5,
  input  B6,
  input  B7,
  input  B8,
  input  B9,
  input  B10,
  input  B11,
  input  D0,
  input  D1,
  input  D2,
  input  D3,
  input  D4,
  input  D5,
  input  D6,
  input  D7,
  input  E,
  input  [15:0] DR_in,
  input  [15:0] AC_in,
  output AR_load,
  output DR_load,
  output AC_load,
  output AR_inr,
  output DR_inr,
  output AC_inr,
  output IR_load,
  output AC_clr,
  output PC_inr,
  output PC_load,
  output [2:0] S2_S1_S0,
  output Memory_read,
  output Memory_write,
  output SC_clr,
  output [2:0] P2_P1_P0,
  output E_clr,
  output E_compliment,
  output E_load,
  output r
);

  wire A1, A2, A3, A4, A5, A6, and_1_out, and_2_out, and_4_out, and_5_out, and_6_out, and_7_out, and_8_out,
       and_9_out, and_10_out, and_11_out, and_12_out, and_13_out, and_14_out, and_15_out, and_18_out,
       and_19_out, and_20_out, and_22_out, and_24_out, and_25_out, and_26_out, and_27_out, and_28_out,
       and_29_out, and_30_out, and_31_out, and_32_out, and_35_out, and_36_out, and_37_out, and_44_out,
       and_45_out, and_46_out, and_47_out, and_48_out, and_49_out, and_50_out, and_51_out, and_52_out,
       and_53_out, and_54_out, and_55_out, and_56_out, and_57_out, and_58_out, and_60_out, if_AC_0, if_DR_0,
       multiplexer_1_out, multiplexer_2_out, multiplexer_3_out, multiplexer_4_out, not_1_out, not_2_out,
       not_3_out, not_4_out, x1, x2, x3, x4, x5, x7;

  not not_1 (not_1_out, I);
  not not_2 (not_2_out, D7);
  and and_1 (and_1_out, D4, T4);
  and and_2 (and_2_out, D5, T5);
  and and_3 (x4, D3, T4);
  and and_4 (and_4_out, D2, T5);
  and and_5 (and_5_out, D6, T6);
  and and_6 (and_6_out, D3, T4);
  and and_7 (and_7_out, D5, T4);
  and and_8 (and_8_out, D6, T6);
  and and_9 (and_9_out, D0, T5);
  and and_10 (and_10_out, D1, T5);
  and and_11 (and_11_out, D2, T5);
  and and_12 (and_12_out, D3, T4);
  and and_13 (and_13_out, D4, T4);
  and and_14 (and_14_out, D5, T5);
  and and_15 (and_15_out, D6, T6);
  and and_16 (E_clr, r, B10);
  and and_17 (E_compliment, r, B8);
  and and_18 (and_18_out, D1, T5);
  and and_19 (and_19_out, r, B7);
  and and_20 (and_20_out, r, B6);
  and and_21 (r, D7, not_1_out, T3);
  and and_22 (and_22_out, not_2_out, I, T3);
  and and_23 (AR_inr, D5, T4);
  and and_24 (and_24_out, D4, T4);
  and and_25 (and_25_out, D5, T5);
  or or_1 (x1, and_1_out, and_2_out);
  or or_2 (x3, and_4_out, and_5_out);
  or or_3 (Memory_write, and_6_out, and_7_out, and_8_out);
  or or_4 (E_load, and_18_out, and_19_out, and_20_out);
  or or_5 (AR_load, and_22_out, T2, T0);
  or or_6 (PC_load, and_24_out, and_25_out);
  or or_7 (SC_clr, and_9_out, and_10_out, and_11_out, and_12_out, and_13_out, and_14_out, and_15_out, r);
  nor nor_1 (if_DR_0, DR_in[0], DR_in[1], DR_in[2], DR_in[3], DR_in[4], DR_in[5], DR_in[6], DR_in[7], DR_in[8], DR_in[9], DR_in[10], DR_in[11], DR_in[12], DR_in[13], DR_in[14], DR_in[15]);
  nor nor_2 (if_AC_0, AC_in[0], AC_in[1], AC_in[2], AC_in[3], AC_in[4], AC_in[5], AC_in[6], AC_in[7], AC_in[8], AC_in[9], AC_in[10], AC_in[11], AC_in[12], AC_in[13], AC_in[14], AC_in[15]);
  and and_26 (and_26_out, D5, T4);
  buf buffer_1 (x5, T2);
  or or_8 (x2, T0, and_26_out);
  and and_27 (and_27_out, D0, T5);
  and and_28 (and_28_out, T5, D1);
  and and_29 (and_29_out, T5, D2);
  and and_30 (and_30_out, r, B9);
  and and_31 (and_31_out, r, B7);
  and and_32 (and_32_out, r, B6);
  and and_33 (AC_inr, r, B5);
  and and_34 (AC_clr, r, B11);
  and and_35 (and_35_out, r, B2);
  and and_36 (and_36_out, r, B4);
  and and_37 (and_37_out, r, B3);
  and and_38 (A1, D2, T5);
  and and_39 (A2, D0, T5);
  and and_40 (A3, D1, T5);
  and and_41 (A4, r, B9);
  and and_42 (A5, r, B7);
  and and_43 (A6, r, B6);
  not not_3 (not_3_out, D7);
  and and_44 (and_44_out, D0, T4);
  and and_45 (and_45_out, D1, T4);
  and and_46 (and_46_out, D2, T4);
  and and_47 (and_47_out, D6, T4);
  Multiplexer multiplexer_1 (.in0(1'b0), .in1(and_35_out), .out(multiplexer_1_out), .sel(if_AC_0));
  Multiplexer multiplexer_2 (.in0(and_36_out), .in1(and_37_out), .out(multiplexer_2_out), .sel(AC_in[15]));
  not not_4 (not_4_out, D7);
  and and_48 (and_48_out, not_3_out, I, T3);
  or or_9 (AC_load, and_27_out, and_28_out, and_29_out, and_30_out, and_31_out, and_32_out);
  and and_49 (and_49_out, D0, T4);
  and and_50 (and_50_out, D1, T4);
  and and_51 (and_51_out, D2, T4);
  and and_52 (and_52_out, D6, T4);
  and and_53 (and_53_out, D6, T6);
  and and_54 (and_54_out, not_4_out, I, T3);
  or or_10 (Memory_read, and_48_out, T1, and_44_out, and_45_out, and_46_out, and_47_out);
  Multiplexer multiplexer_3 (.in0(1'b0), .in1(and_53_out), .out(multiplexer_3_out), .sel(if_DR_0));
  and and_55 (and_55_out, D0, T4);
  and and_56 (and_56_out, D1, T4);
  and and_57 (and_57_out, D2, T4);
  and and_58 (and_58_out, D6, T4);
  buf buffer_2 (IR_load, T1);
  or or_11 (x7, and_54_out, T1, and_49_out, and_50_out, and_51_out, and_52_out);
  or or_12 (P2_P1_P0[0], A1, A2, A5);
  or or_13 (P2_P1_P0[1], A1, A3, A6);
  or or_14 (P2_P1_P0[2], A4, A5, A6);
  and and_59 (DR_inr, D6, T5);
  and and_60 (and_60_out, r, B1);
  or or_15 (DR_load, and_55_out, and_56_out, and_57_out, and_58_out);
  Multiplexer multiplexer_4 (.in0(and_60_out), .in1(1'b0), .out(multiplexer_4_out), .sel(E));
  or or_16 (PC_inr, T1, multiplexer_1_out, multiplexer_2_out, multiplexer_3_out, multiplexer_4_out);
  or or_17 (S2_S1_S0[0], x1, x3, x5, x7);
  or or_18 (S2_S1_S0[1], x2, x3, x7);
  or or_19 (S2_S1_S0[2], x4, x5, x7);

  // Other names for the same wires on the sheet: if_AC_15 = AC_in[15]

  // Notes on the sheet:
  //   E_CONTROL
  //   SC_CONTROL
  //   __________________________________________________________________
  //   __________________________________________________________________
  //   AR
  //   MEMORY CONTROL
  //   __________________________________________________________________
  //   r
  //   COMMON BUS CONTROL
  //   ________________________________________________________________________________________________________________________________________________________
  //   _________________________________________________________________________________________________________________________________________________
  //   ALU CONTROL
  //   _________________________________________________________________________________________________________________________________________________
  //   __________________________________________________________________
  //   AC
  //   IR
  //   PC
  //   DR
endmodule

module Sequence_Counter (
  input  clr,
  input  Start_pulse,
  input  r,
  input  clk,
  input  B0,
  output [3:0] SC_out
);

  wire s_flip_flop_1_sc_inr;
  wire [3:0] adder_1_out, multiplexer_1_out, multiplexer_2_out;

  Adder #(.width(4)) adder_1 (.a(4'b0001), .b(SC_out), .out(adder_1_out));  // open: cin, cout
  S_flip_flop s_flip_flop_1 (.Start_pluse(Start_pulse), .r(r), .B0(B0), .clk(clk), .SC_inr(s_flip_flop_1_sc_inr));
  Multiplexer #(.width(4)) multiplexer_1 (
    .in0(SC_out), .in1(adder_1_out), .out(multiplexer_1_out), .sel(s_flip_flop_1_sc_inr));
  Multiplexer #(.width(4)) multiplexer_2 (.in0(multiplexer_1_out), .in1(4'b0000), .out(multiplexer_2_out), .sel(clr));
  Register #(.width(4)) register_1 (.D(multiplexer_2_out), .en(1'b1), .clk(clk), .Q(SC_out), .clr(1'b0));
endmodule

module E_flip_flop (
  input  E_load,
  input  clk,
  input  E_compliment,
  input  E_clr,
  input  E_inr,
  output E_out
);

  wire multiplexer_1_out, multiplexer_2_out, multiplexer_3_out, not_1_out;

  Multiplexer multiplexer_1 (.in0(E_out), .in1(not_1_out), .out(multiplexer_1_out), .sel(E_compliment));
  not not_1 (not_1_out, E_out);
  Multiplexer multiplexer_2 (.in0(multiplexer_1_out), .in1(E_inr), .out(multiplexer_2_out), .sel(E_load));
  Multiplexer multiplexer_3 (.in0(multiplexer_2_out), .in1(1'b0), .out(multiplexer_3_out), .sel(E_clr));
  D_Flip_Flop d_ff_1 (.D(multiplexer_3_out), .clk(clk), .Q(E_out));  // open: Qn, preset, reset
endmodule

module S_flip_flop (
  input  Start_pluse,
  input  r,
  input  B0,
  input  clk,
  output SC_inr
);

  wire and_1_out, and_2_out, not_1_out, or_1_out;

  and and_1 (and_1_out, r, B0);
  not not_1 (not_1_out, and_1_out);
  and and_2 (and_2_out, not_1_out, SC_inr);
  or or_1 (or_1_out, Start_pluse, and_2_out);
  D_Flip_Flop d_ff_1 (.D(or_1_out), .clk(clk), .Q(SC_inr));  // open: Qn, preset, reset
endmodule
